# Fritzing sketch circuit (saved by Fritzing 0.7.12b)
breadboards: 2

parts:
  Arduino_Ethernet_Shield1 = Arduino Ethernet Shield
  R1 = Resistor [tolerance=±5% resistance=10k package=THT]
  T1 = LM35 Temperature Sensor [package="TO92 [THT]"]
  R2 = Photocell (LDR) [package=THT]
  R3 = Resistor [tolerance=±5% resistance=10k package=THT]
  Power_plug1 = Power plug
  K1 = Relay [part_number=FRS1B-S package=THT]
  R4 = Resistor [tolerance=±5% resistance=330 package=THT]
  D1 = Rectifier Diode [part_number=1N4001 package="300 mil [THT]"]
  D2 = Rectifier Diode [part_number=1N4001 package="300 mil [THT]"]
  M1 = DC Motor

nets:
  N1: Arduino_Ethernet_Shield1.D5, R4.Pin_1
  N2: Arduino_Ethernet_Shield1.D3, R1.Pin_0
  N3: Arduino_Ethernet_Shield1.+5V, T1.+Vs, R3.Pin_1
  GND: Arduino_Ethernet_Shield1.GND, T1.GND, R2.pin_0
  N4: Arduino_Ethernet_Shield1.A0, T1.Vout
  N5: Arduino_Ethernet_Shield1.A1, R2.pin_1, R3.Pin_0
  N6: Arduino_Ethernet_Shield1.A2, R1.Pin_1
  N7: Power_plug1.VCC, K1.B
  N8: Power_plug1.GND, D2.anode, M1.pin_2
  N9: K1.COIL1, D1.cathode
  N10: K1.C1, K1.C2, D2.cathode, M1.pin_1
  N11: K1.COIL2, R4.Pin_0, D1.anode
